// Logisim project PROJECTLOGISIM.circ as structural Verilog: 1 circuit, main circuit main
module main (
  input  A,
  input  B,
  input  C,
  input  A_2,
  input  B_2,
  input  C_2
);

  wire and_1_out, and_2_out, and_3_out, and_4_out, and_5_out, nand_1_out, nand_2_out, nand_3_out, nand_4_out,
       nand_5_out, nand_6_out, nand_7_out, nand_8_out, nand_9_out, nand_10_out, nand_11_out, nand_12_out,
       nand_13_out, nand_14_out, nand_15_out, nand_16_out, nand_17_out, nand_18_out, nand_19_out, not_1_out,
       not_2_out, not_3_out, or_1_out;

  not not_1 (not_1_out, A);
  not not_2 (not_2_out, B);
  not not_3 (not_3_out, C);
  and and_1 (and_1_out, A, B, C);
  and and_2 (and_2_out, not_1_out, B, C);
  and and_3 (and_3_out, A, not_2_out, not_3_out);
  and and_4 (and_4_out, A, not_2_out, C);
  and and_5 (and_5_out, not_1_out, not_2_out, C);
  or or_1 (or_1_out, and_1_out, and_2_out, and_3_out, and_4_out, and_5_out);
  LED led_1 (.in(or_1_out));
  nand nand_1 (nand_1_out, A_2, A_2);
  nand nand_2 (nand_2_out, B_2, B_2);
  nand nand_3 (nand_3_out, C_2, C_2);
  nand nand_4 (nand_4_out, A_2, B_2, C_2);
  nand nand_5 (nand_5_out, nand_1_out, B_2, C_2);
  nand nand_6 (nand_6_out, A_2, nand_2_out, nand_3_out);
  nand nand_7 (nand_7_out, A_2, nand_2_out, C_2);
  nand nand_8 (nand_8_out, nand_1_out, nand_2_out, C_2);
  nand nand_9 (nand_9_out, nand_4_out, nand_4_out);
  nand nand_10 (nand_10_out, nand_5_out, nand_5_out);
  nand nand_11 (nand_11_out, nand_6_out, nand_6_out);
  nand nand_12 (nand_12_out, nand_7_out, nand_7_out);
  nand nand_13 (nand_13_out, nand_8_out, nand_8_out);
  nand nand_14 (nand_14_out, nand_9_out, nand_9_out);
  nand nand_15 (nand_15_out, nand_10_out, nand_10_out);
  nand nand_16 (nand_16_out, nand_11_out, nand_11_out);
  nand nand_17 (nand_17_out, nand_12_out, nand_12_out);
  nand nand_18 (nand_18_out, nand_13_out, nand_13_out);
  nand nand_19 (nand_19_out, nand_14_out, nand_15_out, nand_16_out, nand_17_out, nand_18_out);
  LED led_2 (.in(nand_19_out));

  // Notes on the sheet:
  //   AND-OR:
  //   f(A,B,C) = ABC+A’BC+AB’C’+AB’C+A’B’C
  //   ABC
  //   A'BC
  //   AB'C'
  //   AB'C
  //   A'B'C
  //   NAND:
  //   f(A,B,C) = ABC+A’BC+AB’C’+AB’C+A’B’C
  //   ABC
  //   A'BC
  //   AB'C'
  //   AB'C
  //   A'B'C
  //   AND gates
  //   OR gates
endmodule
